# Fritzing sketch code_lijn_volg_robot (saved by Fritzing 0.9.3b)
breadboards: 1

parts:
  Onderdeel1 = Arduino Uno (Rev3) - ICSP
  M1 = fc-51 [package=THT]
  M2 = fc-51 [package=THT]
  M3 = fc-51 [package=THT]
  M4 = fc-51 [package=THT]
  HC-SR04_Sensor_1 = HC-SR04 Ultrasonic Distance Sensor
  M5 = DC Motor
  M6 = DC Motor
  IC1 = L293D [package=THT]

nets:
  N1: Onderdeel1.ICSP_MISO, Onderdeel1.D12/MISO, HC-SR04_Sensor_1.ECHO
  N2: Onderdeel1.D8, IC1.In_1
  N3: Onderdeel1.D9_PWM, IC1.In_2
  N4: Onderdeel1.D10_PWM/SS, M3.pin1
  N5: Onderdeel1.D11_PWM/MOSI, M4.pin1
  N6: Onderdeel1.D13/SCK, HC-SR04_Sensor_1.TRIG
  N7: Onderdeel1.D4, IC1.In_3
  N8: Onderdeel1.D5_PWM, IC1.In_4
  N9: Onderdeel1.D6_PWM, M2.pin1
  N10: Onderdeel1.D7, M1.pin1
  5V: Onderdeel1.5V, M1.pin3, M2.pin3, M3.pin3, M4.pin3, HC-SR04_Sensor_1.VCC, IC1.Enable_1, IC1.+Vmotor, IC1.Enable_2, IC1.+V
  GND: Onderdeel1.GND, M1.pin2, M2.pin2, M3.pin2, M4.pin2, HC-SR04_Sensor_1.GND, IC1.0V
  N11: M5.pin_1, IC1.Out_4_(_Controlled_by_Enable_2_)
  N12: M5.pin_2, IC1.Out_3_(_Controlled_by_Enable_2_)
  N13: M6.pin_1, IC1.Out_2_(_Controlled_by_Enable_1_)
  N14: M6.pin_2, IC1.Out_1_(_Controlled_by_Enable_1_)
